// Logisim project CircuitoAnd.circ as structural Verilog: 1 circuit, main circuit main
module main (
  input  A,
  input  B,
  input  A_2,
  input  B_2,
  input  A_3,
  input  B_3,
  input  A_4,
  input  B_4,
  output out_9,
  output out_10,
  output out_11,
  output out_12
);

  wire and_1_out, and_2_out, and_3_out, and_4_out;

  and and_1 (and_1_out, A, B);
  not not_1 (out_10, and_2_out);
  and and_2 (and_2_out, A_2, B_2);
  and and_3 (and_3_out, A_3, B_3);
  and and_4 (and_4_out, A_4, B_4);
  not not_2 (out_9, and_1_out);
  not not_3 (out_11, and_3_out);
  not not_4 (out_12, and_4_out);
endmodule
